// Logisim project 1b Processor.circ as structural Verilog: 3 circuits, main circuit main
module main (
  input  in_1,
  input  in_2,
  input  in_3,
  input  in_4
);

  wire [2:0] adder_1_out, register_1_q;

  Adder #(.width(3)) adder_1 (.a(register_1_q), .b(3'b001), .out(adder_1_out));  // open: cin, cout
  Register #(.width(3)) register_1 (.D(adder_1_out), .Q(register_1_q), .clk(in_2), .clr(in_3));  // open: en
  // Program_Counter program_counter_1: pin names not known; wires that end beside it: register_1_q, in_2, in_3
  ROM rom_1 ();  // open: addr, data, sel
endmodule

module _8_by_1_register (
  input  Clock,
  input  [2:0] Address,
  input  Data_In,
  output out_4
);

  wire controlled_buffer_1_out, controlled_buffer_2_out, controlled_buffer_3_out, controlled_buffer_4_out,
       controlled_buffer_5_out, controlled_buffer_6_out, controlled_buffer_7_out, controlled_buffer_8_out,
       d_ff_1_q, d_ff_2_q, d_ff_3_q, d_ff_4_q, d_ff_5_q, d_ff_6_q, d_ff_7_q, d_ff_8_q, decoder_1_out0,
       decoder_1_out1, decoder_1_out2, decoder_1_out3, decoder_1_out4, decoder_1_out5, decoder_1_out6,
       decoder_1_out7;

  Decoder #(.select(3), .disabled(0), .enable("false")) decoder_1 (
    .out0(decoder_1_out0), .out1(decoder_1_out1), .out2(decoder_1_out2), .out3(decoder_1_out3),
    .out4(decoder_1_out4), .out5(decoder_1_out5), .out6(decoder_1_out6), .out7(decoder_1_out7), .sel(Address));
  assign controlled_buffer_1_out = decoder_1_out0 ? Data_In : 1'bz;  // Controlled_Buffer controlled_buffer_1
  assign controlled_buffer_2_out = decoder_1_out1 ? Data_In : 1'bz;  // Controlled_Buffer controlled_buffer_2
  assign controlled_buffer_3_out = decoder_1_out2 ? Data_In : 1'bz;  // Controlled_Buffer controlled_buffer_3
  assign controlled_buffer_4_out = decoder_1_out3 ? Data_In : 1'bz;  // Controlled_Buffer controlled_buffer_4
  assign controlled_buffer_5_out = decoder_1_out4 ? Data_In : 1'bz;  // Controlled_Buffer controlled_buffer_5
  assign controlled_buffer_6_out = decoder_1_out5 ? Data_In : 1'bz;  // Controlled_Buffer controlled_buffer_6
  assign controlled_buffer_7_out = decoder_1_out6 ? Data_In : 1'bz;  // Controlled_Buffer controlled_buffer_7
  assign controlled_buffer_8_out = decoder_1_out7 ? Data_In : 1'bz;  // Controlled_Buffer controlled_buffer_8
  assign out_4 = decoder_1_out0 ? d_ff_1_q : 1'bz;  // Controlled_Buffer controlled_buffer_9
  D_Flip_Flop d_ff_1 (
    .clk(Clock), .D(controlled_buffer_1_out), .Q(d_ff_1_q), .en(decoder_1_out0));  // open: Qn, preset, reset
  D_Flip_Flop d_ff_2 (
    .clk(Clock), .D(controlled_buffer_2_out), .Q(d_ff_2_q), .en(decoder_1_out1));  // open: Qn, preset, reset
  assign out_4 = decoder_1_out1 ? d_ff_2_q : 1'bz;  // Controlled_Buffer controlled_buffer_10
  D_Flip_Flop d_ff_3 (
    .clk(Clock), .D(controlled_buffer_3_out), .Q(d_ff_3_q), .en(decoder_1_out2));  // open: Qn, preset, reset
  assign out_4 = decoder_1_out2 ? d_ff_3_q : 1'bz;  // Controlled_Buffer controlled_buffer_11
  D_Flip_Flop d_ff_4 (
    .clk(Clock), .D(controlled_buffer_4_out), .Q(d_ff_4_q), .en(decoder_1_out3));  // open: Qn, preset, reset
  assign out_4 = decoder_1_out3 ? d_ff_4_q : 1'bz;  // Controlled_Buffer controlled_buffer_12
  D_Flip_Flop d_ff_5 (
    .clk(Clock), .D(controlled_buffer_5_out), .Q(d_ff_5_q), .en(decoder_1_out4));  // open: Qn, preset, reset
  assign out_4 = decoder_1_out4 ? d_ff_5_q : 1'bz;  // Controlled_Buffer controlled_buffer_13
  D_Flip_Flop d_ff_6 (
    .clk(Clock), .D(controlled_buffer_6_out), .Q(d_ff_6_q), .en(decoder_1_out5));  // open: Qn, preset, reset
  assign out_4 = decoder_1_out5 ? d_ff_6_q : 1'bz;  // Controlled_Buffer controlled_buffer_14
  assign out_4 = decoder_1_out6 ? d_ff_7_q : 1'bz;  // Controlled_Buffer controlled_buffer_15
  D_Flip_Flop d_ff_7 (
    .clk(Clock), .D(controlled_buffer_7_out), .Q(d_ff_7_q), .en(decoder_1_out6));  // open: Qn, preset, reset
  D_Flip_Flop d_ff_8 (
    .clk(Clock), .D(controlled_buffer_8_out), .Q(d_ff_8_q), .en(decoder_1_out7));  // open: Qn, preset, reset
  assign out_4 = decoder_1_out7 ? d_ff_8_q : 1'bz;  // Controlled_Buffer controlled_buffer_16
endmodule

module Program_Counter (
  input  Clear,
  input  Clock,
  input  Set,
  input  [2:0] Address,
  input  Data_In,
  output out_6,
  output out_7,
  output out_8,
  output out_9,
  output out_10,
  output out_11,
  output out_12,
  output out_13
);

  wire adder_1_cout, adder_1_out, adder_2_cout, adder_2_out, adder_3_cout, adder_3_out, adder_4_cout,
       adder_4_out, adder_5_cout, adder_5_out, adder_6_cout, adder_6_out, adder_7_cout, adder_7_out,
       adder_8_out, controlled_buffer_1_out, controlled_buffer_2_out, controlled_buffer_3_out,
       controlled_buffer_4_out, controlled_buffer_5_out, controlled_buffer_6_out, controlled_buffer_7_out,
       controlled_buffer_8_out, d_ff_1_qn, d_ff_2_qn, d_ff_3_qn, d_ff_4_qn, d_ff_5_qn, d_ff_6_qn, d_ff_7_qn,
       d_ff_8_qn, decoder_1_out0, decoder_1_out1, decoder_1_out2, decoder_1_out3, decoder_1_out4,
       decoder_1_out5, decoder_1_out6, decoder_1_out7, not_1_out, not_2_out, not_3_out, not_4_out, not_5_out,
       not_6_out, not_7_out, not_8_out, not_9_out, or_1_out, or_2_out, or_3_out, or_4_out, or_5_out,
       or_6_out, or_7_out, or_8_out;

  Decoder #(.select(3), .disabled(0)) decoder_1 (
    .out0(decoder_1_out0), .out1(decoder_1_out1), .out2(decoder_1_out2), .out3(decoder_1_out3),
    .out4(decoder_1_out4), .out5(decoder_1_out5), .out6(decoder_1_out6), .out7(decoder_1_out7),
    .sel(Address), .en(Set));
  assign controlled_buffer_1_out = decoder_1_out0 ? Data_In : 1'bz;  // Controlled_Buffer controlled_buffer_1
  assign controlled_buffer_2_out = decoder_1_out1 ? Data_In : 1'bz;  // Controlled_Buffer controlled_buffer_2
  assign controlled_buffer_3_out = decoder_1_out2 ? Data_In : 1'bz;  // Controlled_Buffer controlled_buffer_3
  assign controlled_buffer_4_out = decoder_1_out3 ? Data_In : 1'bz;  // Controlled_Buffer controlled_buffer_4
  assign controlled_buffer_5_out = decoder_1_out4 ? Data_In : 1'bz;  // Controlled_Buffer controlled_buffer_5
  assign controlled_buffer_6_out = decoder_1_out5 ? Data_In : 1'bz;  // Controlled_Buffer controlled_buffer_6
  assign controlled_buffer_7_out = decoder_1_out6 ? Data_In : 1'bz;  // Controlled_Buffer controlled_buffer_7
  assign controlled_buffer_8_out = decoder_1_out7 ? Data_In : 1'bz;  // Controlled_Buffer controlled_buffer_8
  D_Flip_Flop d_ff_1 (
    .clk(Clock), .D(controlled_buffer_1_out), .Q(out_6), .Qn(d_ff_1_qn), .en(or_1_out), .reset(Clear));  // open: preset
  or or_1 (or_1_out, decoder_1_out0, not_1_out);
  D_Flip_Flop d_ff_2 (
    .clk(Clock), .D(controlled_buffer_2_out), .Q(out_7), .Qn(d_ff_2_qn), .en(or_2_out), .reset(Clear));  // open: preset
  or or_2 (or_2_out, decoder_1_out1, not_1_out);
  D_Flip_Flop d_ff_3 (
    .clk(Clock), .D(controlled_buffer_3_out), .Q(out_8), .Qn(d_ff_3_qn), .en(or_3_out), .reset(Clear));  // open: preset
  or or_3 (or_3_out, decoder_1_out2, not_1_out);
  D_Flip_Flop d_ff_4 (
    .clk(Clock), .D(controlled_buffer_4_out), .Q(out_9), .Qn(d_ff_4_qn), .en(or_4_out), .reset(Clear));  // open: preset
  or or_4 (or_4_out, decoder_1_out3, not_1_out);
  D_Flip_Flop d_ff_5 (
    .clk(Clock), .D(controlled_buffer_5_out), .Q(out_10), .Qn(d_ff_5_qn), .en(or_5_out), .reset(Clear));  // open: preset
  or or_5 (or_5_out, decoder_1_out4, not_1_out);
  D_Flip_Flop d_ff_6 (
    .clk(Clock), .D(controlled_buffer_6_out), .Q(out_11), .Qn(d_ff_6_qn), .en(or_6_out), .reset(Clear));  // open: preset
  or or_6 (or_6_out, decoder_1_out5, not_1_out);
  D_Flip_Flop d_ff_7 (
    .clk(Clock), .D(controlled_buffer_7_out), .Q(out_12), .Qn(d_ff_7_qn), .en(or_7_out), .reset(Clear));  // open: preset
  or or_7 (or_7_out, decoder_1_out6, not_1_out);
  D_Flip_Flop d_ff_8 (
    .clk(Clock), .D(controlled_buffer_8_out), .Q(out_13), .Qn(d_ff_8_qn), .en(or_8_out), .reset(Clear));  // open: preset
  or or_8 (or_8_out, decoder_1_out7, not_1_out);
  not not_1 (not_1_out, Set);
  Adder #(.width(1)) adder_1 (.a(1'b1), .b(not_2_out), .out(adder_1_out), .cout(adder_1_cout));  // open: cin
  not not_2 (not_2_out, d_ff_1_qn);
  Adder #(.width(1)) adder_2 (.a(1'b0), .b(not_3_out), .out(adder_2_out), .cin(adder_1_cout), .cout(adder_2_cout));
  not not_3 (not_3_out, d_ff_2_qn);
  Adder #(.width(1)) adder_3 (.a(1'b0), .b(not_4_out), .out(adder_3_out), .cin(adder_2_cout), .cout(adder_3_cout));
  not not_4 (not_4_out, d_ff_3_qn);
  Adder #(.width(1)) adder_4 (.a(1'b0), .b(not_5_out), .out(adder_4_out), .cin(adder_3_cout), .cout(adder_4_cout));
  not not_5 (not_5_out, d_ff_4_qn);
  Adder #(.width(1)) adder_5 (.a(1'b0), .b(not_6_out), .out(adder_5_out), .cin(adder_4_cout), .cout(adder_5_cout));
  not not_6 (not_6_out, d_ff_5_qn);
  Adder #(.width(1)) adder_6 (.a(1'b0), .b(not_7_out), .out(adder_6_out), .cin(adder_5_cout), .cout(adder_6_cout));
  not not_7 (not_7_out, d_ff_6_qn);
  Adder #(.width(1)) adder_7 (.a(1'b0), .b(not_8_out), .out(adder_7_out), .cin(adder_6_cout), .cout(adder_7_cout));
  not not_8 (not_8_out, d_ff_7_qn);
  Adder #(.width(1)) adder_8 (.a(1'b0), .b(not_9_out), .out(adder_8_out), .cin(adder_7_cout));  // open: cout
  not not_9 (not_9_out, d_ff_8_qn);
  assign controlled_buffer_1_out = not_1_out ? adder_1_out : 1'bz;  // Controlled_Buffer controlled_buffer_9
  assign controlled_buffer_2_out = not_1_out ? adder_2_out : 1'bz;  // Controlled_Buffer controlled_buffer_10
  assign controlled_buffer_3_out = not_1_out ? adder_3_out : 1'bz;  // Controlled_Buffer controlled_buffer_11
  assign controlled_buffer_4_out = not_1_out ? adder_4_out : 1'bz;  // Controlled_Buffer controlled_buffer_12
  assign controlled_buffer_5_out = not_1_out ? adder_5_out : 1'bz;  // Controlled_Buffer controlled_buffer_13
  assign controlled_buffer_6_out = not_1_out ? adder_6_out : 1'bz;  // Controlled_Buffer controlled_buffer_14
  assign controlled_buffer_7_out = not_1_out ? adder_7_out : 1'bz;  // Controlled_Buffer controlled_buffer_15
  Controlled_Buffer controlled_buffer_16 (.in(adder_8_out), .en(not_1_out));  // open: out
endmodule
