// Logisim project 8 Bit Parallel Processor.circ as structural Verilog: 3 circuits, main circuit main
module main (
  input  in_1,
  output [1:0] out_2,
  output [1:0] out_3,
  output [1:0] out_4,
  output [1:0] out_5
);

  wire clock_1_out, multiplexer_1_out, multiplexer_2_out, multiplexer_6_out, multiplexer_7_out,
       multiplexer_11_out, multiplexer_12_out, multiplexer_16_out, multiplexer_17_out,
       Processor_A_external_read, Processor_A_external_write, Processor_B_external_read,
       Processor_B_external_write, Processor_C_external_read, Processor_C_external_write,
       Processor_D_external_read, Processor_D_external_write;
  wire [7:0] Channel_A_data_out, Channel_B_data_out, Channel_C_data_out, Channel_D_data_out,
       multiplexer_3_out, multiplexer_5_out, multiplexer_8_out, multiplexer_10_out, multiplexer_13_out,
       multiplexer_15_out, multiplexer_18_out, multiplexer_20_out, Processor_A_data_out, Processor_A_mar,
       Processor_B_data_out, Processor_B_mar, Processor_C_data_out, Processor_C_mar, Processor_D_data_out,
       Processor_D_mar;

  Clock clock_1 (.out(clock_1_out));
  Multiplexer #(.select(2), .enable("false")) multiplexer_1 (
    .in0(Processor_A_external_read), .in1(Processor_B_external_read), .in2(Processor_C_external_read),
    .in3(Processor_D_external_read), .out(multiplexer_1_out), .sel(out_2));
  Multiplexer #(.select(2), .enable("false")) multiplexer_2 (
    .in0(Processor_A_external_write), .in1(Processor_B_external_write), .in2(Processor_C_external_write),
    .in3(Processor_D_external_write), .out(multiplexer_2_out), .sel(out_2));
  Multiplexer #(.select(2), .width(8), .enable("false")) multiplexer_3 (
    .in0(Processor_A_mar), .in1(Processor_B_mar), .in2(Processor_C_mar), .in3(Processor_D_mar),
    .out(multiplexer_3_out), .sel(out_2));
  Counter #(.width(2), .max('h3)) counter_1 (.Q(out_2), .clk(clock_1_out), .clr(in_1));  // open: load, D, count, carry
  Global_Cluster Channel_A (
    .Read(multiplexer_1_out), .Write(multiplexer_2_out), .Mar(multiplexer_3_out),
    .Data_In(multiplexer_5_out), .Clock(clock_1_out), .Counter(out_2), .Data_Out(Channel_A_data_out));
  Multiplexer #(.select(2), .width(8)) multiplexer_4 (
    .in0(Processor_A_data_out), .in1(Processor_B_data_out), .in2(Processor_C_data_out),
    .in3(Processor_D_data_out), .out(Channel_A_data_out), .sel(out_2), .en(multiplexer_1_out));
  Multiplexer #(.select(2), .width(8)) multiplexer_5 (
    .in0(Processor_A_data_out), .in1(Processor_B_data_out), .in2(Processor_C_data_out),
    .in3(Processor_D_data_out), .out(multiplexer_5_out), .sel(out_2), .en(multiplexer_2_out));
  _8_Bit_Processor Processor_A (
    .Clock(clock_1_out), .Clear(in_1), .Data_In(Processor_A_data_out),
    .External_Read(Processor_A_external_read), .Mar(Processor_A_mar), .Data_Out(Processor_A_data_out),
    .External_Write(Processor_A_external_write));
  Multiplexer #(.select(2), .enable("false")) multiplexer_6 (
    .in0(Processor_A_external_read), .in1(Processor_B_external_read), .in2(Processor_C_external_read),
    .in3(Processor_D_external_read), .out(multiplexer_6_out), .sel(out_3));
  Multiplexer #(.select(2), .enable("false")) multiplexer_7 (
    .in0(Processor_A_external_write), .in1(Processor_B_external_write), .in2(Processor_C_external_write),
    .in3(Processor_D_external_write), .out(multiplexer_7_out), .sel(out_3));
  Multiplexer #(.select(2), .width(8), .enable("false")) multiplexer_8 (
    .in0(Processor_A_mar), .in1(Processor_B_mar), .in2(Processor_C_mar), .in3(Processor_D_mar),
    .out(multiplexer_8_out), .sel(out_3));
  Adder #(.width(2)) adder_1 (.a(out_2), .b(2'b01), .out(out_3));  // open: cin, cout
  Global_Cluster Channel_B (
    .Read(multiplexer_6_out), .Write(multiplexer_7_out), .Mar(multiplexer_8_out),
    .Data_In(multiplexer_10_out), .Clock(clock_1_out), .Counter(out_3), .Data_Out(Channel_B_data_out));
  Multiplexer #(.select(2), .width(8)) multiplexer_9 (
    .in0(Processor_A_data_out), .in1(Processor_B_data_out), .in2(Processor_C_data_out),
    .in3(Processor_D_data_out), .out(Channel_B_data_out), .sel(out_3), .en(multiplexer_6_out));
  Multiplexer #(.select(2), .width(8)) multiplexer_10 (
    .in0(Processor_A_data_out), .in1(Processor_B_data_out), .in2(Processor_C_data_out),
    .in3(Processor_D_data_out), .out(multiplexer_10_out), .sel(out_3), .en(multiplexer_7_out));
  _8_Bit_Processor Processor_B (
    .Clock(clock_1_out), .Clear(in_1), .Data_In(Processor_B_data_out),
    .External_Read(Processor_B_external_read), .Mar(Processor_B_mar), .Data_Out(Processor_B_data_out),
    .External_Write(Processor_B_external_write));
  Multiplexer #(.select(2), .enable("false")) multiplexer_11 (
    .in0(Processor_A_external_read), .in1(Processor_B_external_read), .in2(Processor_C_external_read),
    .in3(Processor_D_external_read), .out(multiplexer_11_out), .sel(out_4));
  Multiplexer #(.select(2), .enable("false")) multiplexer_12 (
    .in0(Processor_A_external_write), .in1(Processor_B_external_write), .in2(Processor_C_external_write),
    .in3(Processor_D_external_write), .out(multiplexer_12_out), .sel(out_4));
  Multiplexer #(.select(2), .width(8), .enable("false")) multiplexer_13 (
    .in0(Processor_A_mar), .in1(Processor_B_mar), .in2(Processor_C_mar), .in3(Processor_D_mar),
    .out(multiplexer_13_out), .sel(out_4));
  Adder #(.width(2)) adder_2 (.a(out_3), .b(2'b01), .out(out_4));  // open: cin, cout
  Global_Cluster Channel_C (
    .Read(multiplexer_11_out), .Write(multiplexer_12_out), .Mar(multiplexer_13_out),
    .Data_In(multiplexer_15_out), .Clock(clock_1_out), .Counter(out_4), .Data_Out(Channel_C_data_out));
  Multiplexer #(.select(2), .width(8)) multiplexer_14 (
    .in0(Processor_A_data_out), .in1(Processor_B_data_out), .in2(Processor_C_data_out),
    .in3(Processor_D_data_out), .out(Channel_C_data_out), .sel(out_4), .en(multiplexer_11_out));
  Multiplexer #(.select(2), .width(8)) multiplexer_15 (
    .in0(Processor_A_data_out), .in1(Processor_B_data_out), .in2(Processor_C_data_out),
    .in3(Processor_D_data_out), .out(multiplexer_15_out), .sel(out_4), .en(multiplexer_12_out));
  _8_Bit_Processor Processor_C (
    .Clock(clock_1_out), .Clear(in_1), .Data_In(Processor_C_data_out),
    .External_Read(Processor_C_external_read), .Mar(Processor_C_mar), .Data_Out(Processor_C_data_out),
    .External_Write(Processor_C_external_write));
  Multiplexer #(.select(2), .enable("false")) multiplexer_16 (
    .in0(Processor_A_external_read), .in1(Processor_B_external_read), .in2(Processor_C_external_read),
    .in3(Processor_D_external_read), .out(multiplexer_16_out), .sel(out_5));
  Multiplexer #(.select(2), .enable("false")) multiplexer_17 (
    .in0(Processor_A_external_write), .in1(Processor_B_external_write), .in2(Processor_C_external_write),
    .in3(Processor_D_external_write), .out(multiplexer_17_out), .sel(out_5));
  Multiplexer #(.select(2), .width(8), .enable("false")) multiplexer_18 (
    .in0(Processor_A_mar), .in1(Processor_B_mar), .in2(Processor_C_mar), .in3(Processor_D_mar),
    .out(multiplexer_18_out), .sel(out_5));
  Adder #(.width(2)) adder_3 (.a(out_4), .b(2'b01), .out(out_5));  // open: cin, cout
  Global_Cluster Channel_D (
    .Read(multiplexer_16_out), .Write(multiplexer_17_out), .Mar(multiplexer_18_out),
    .Data_In(multiplexer_20_out), .Clock(clock_1_out), .Counter(out_5), .Data_Out(Channel_D_data_out));
  Multiplexer #(.select(2), .width(8)) multiplexer_19 (
    .in0(Processor_A_data_out), .in1(Processor_B_data_out), .in2(Processor_C_data_out),
    .in3(Processor_D_data_out), .out(Channel_D_data_out), .sel(out_5), .en(multiplexer_16_out));
  Multiplexer #(.select(2), .width(8)) multiplexer_20 (
    .in0(Processor_A_data_out), .in1(Processor_B_data_out), .in2(Processor_C_data_out),
    .in3(Processor_D_data_out), .out(multiplexer_20_out), .sel(out_5), .en(multiplexer_17_out));
  _8_Bit_Processor Processor_D (
    .Clock(clock_1_out), .Clear(in_1), .Data_In(Processor_D_data_out),
    .External_Read(Processor_D_external_read), .Mar(Processor_D_mar), .Data_Out(Processor_D_data_out),
    .External_Write(Processor_D_external_write));
endmodule

module Global_Cluster (
  input  Read,
  input  Write,
  input  [7:0] Mar,
  input  [7:0] Data_In,
  input  Clock,
  input  [1:0] Counter,
  output [7:0] Data_Out
);

  wire and_1_out, and_2_out, and_3_out, and_4_out, and_5_out, and_6_out, and_7_out, and_8_out, and_9_out,
       and_10_out, and_11_out, and_12_out, and_13_out, xnor_1_out, xnor_2_out;
  wire [6:0] controlled_buffer_2_out;
  wire [7:0] controlled_buffer_3_out, ram_1_data, register_1_q, register_2_q, register_3_q;

  assign Data_Out = Read ? controlled_buffer_3_out : 8'bz;  // Controlled_Buffer controlled_buffer_1
  xnor xnor_1 (xnor_1_out, Counter[0], Mar[0]);
  and and_1 (and_1_out, xnor_1_out, xnor_2_out);
  xnor xnor_2 (xnor_2_out, Counter[1], Mar[1]);
  and and_2 (and_2_out, and_1_out, Mar[7]);
  assign controlled_buffer_2_out = and_2_out ? Mar[6:0] : 7'bz;  // Controlled_Buffer controlled_buffer_2
  assign controlled_buffer_3_out = Write ? Data_In : 8'bz;  // Controlled_Buffer controlled_buffer_3
  and and_3 (and_3_out, controlled_buffer_2_out[6], Write);
  and and_4 (and_4_out, controlled_buffer_2_out[4], Write);
  and and_5 (and_5_out, Clock, and_8_out);
  and and_6 (and_6_out, Clock, and_3_out);
  and and_7 (and_7_out, Clock, and_4_out);
  Pull_Resistor pull_resistor_1 (.node(controlled_buffer_2_out[6]));
  and and_8 (and_8_out, controlled_buffer_2_out[3], Write);
  and and_9 (and_9_out, controlled_buffer_2_out[6], Read);
  Pull_Resistor pull_resistor_2 (.node(controlled_buffer_2_out[3]));
  Pull_Resistor pull_resistor_3 (.node(controlled_buffer_2_out[4]));
  and and_10 (and_10_out, controlled_buffer_2_out[4], Read);
  and and_11 (and_11_out, controlled_buffer_2_out[3], Read);
  Register register_1 (.D(controlled_buffer_3_out), .Q(register_1_q), .clk(and_5_out));  // open: en, clr
  assign controlled_buffer_3_out = and_11_out ? register_1_q : 8'bz;  // Controlled_Buffer controlled_buffer_4
  Register register_2 (.D(controlled_buffer_3_out), .Q(register_2_q), .clk(and_7_out));  // open: en, clr
  assign controlled_buffer_3_out = and_10_out ? register_2_q : 8'bz;  // Controlled_Buffer controlled_buffer_5
  Register register_3 (.D(controlled_buffer_3_out), .Q(register_3_q), .clk(and_6_out));  // open: en, clr
  assign controlled_buffer_3_out = and_9_out ? register_3_q : 8'bz;  // Controlled_Buffer controlled_buffer_6
  Pull_Resistor pull_resistor_4 (.node(controlled_buffer_2_out[5]));
  RAM #(.addrWidth(16)) ram_1 (
    .addr({register_2_q, register_1_q}), .data(ram_1_data), .sel(controlled_buffer_2_out[5]), .clk(Clock),
    .ld(and_12_out));  // open: clr
  and and_12 (and_12_out, controlled_buffer_2_out[5], Read);
  assign controlled_buffer_3_out = and_12_out ? ram_1_data : 8'bz;  // Controlled_Buffer controlled_buffer_7
  and and_13 (and_13_out, controlled_buffer_2_out[5], Write);
  assign ram_1_data = and_13_out ? controlled_buffer_3_out : 8'bz;  // Controlled_Buffer controlled_buffer_8
endmodule

module _8_Bit_Processor (
  input  Clock,
  input  Clear,
  input  [7:0] Data_In,
  output External_Read,
  output [7:0] Mar,
  output [7:0] Data_Out,
  output External_Write
);

  wire and_1_out, and_2_out, and_3_out, and_4_out, and_5_out, demultiplexer_1_out0, demultiplexer_1_out1,
       demultiplexer_1_out2, demultiplexer_1_out3, demultiplexer_2_out0, demultiplexer_2_out1,
       demultiplexer_3_out0, demultiplexer_3_out1, demultiplexer_3_out3, demultiplexer_3_out4,
       demultiplexer_3_out5, demultiplexer_3_out6, demultiplexer_3_out7, demultiplexer_4_out0,
       demultiplexer_4_out1, demultiplexer_4_out2, demultiplexer_4_out4, demultiplexer_4_out5,
       demultiplexer_4_out6, demultiplexer_4_out7, demultiplexer_4_out8, demultiplexer_4_out9,
       demultiplexer_4_out10, demultiplexer_4_out11, demultiplexer_4_out12, demultiplexer_4_out13,
       demultiplexer_4_out14, demultiplexer_4_out15, nor_1_out, not_2_out, or_1_out, or_3_out;
  wire [6:0] pull_resistor_1_node, register_3_q;
  wire [7:0] adder_1_out, adder_2_out, and_6_out, controlled_buffer_4_out, controlled_buffer_7_out,
       multiplexer_1_out, multiplexer_2_out, multiplexer_3_out, not_1_out, or_2_out, ram_1_data,
       register_1_q, register_2_q, register_4_q, register_5_q, register_6_q, register_7_q, rom_1_data;
  wire [7:7] pull_resistor_1_node_2;

  Pull_Resistor pull_resistor_1 (.node({pull_resistor_1_node_2[7], pull_resistor_1_node}));
  assign {pull_resistor_1_node_2[7], pull_resistor_1_node} = demultiplexer_4_out1 ? register_1_q : 8'bz;  // Controlled_Buffer controlled_buffer_1
  Adder adder_1 (.a(register_2_q), .b(multiplexer_1_out), .out(adder_1_out));  // open: cin, cout
  Multiplexer #(.width(8), .enable("false")) multiplexer_1 (
    .in0(8'h1), .in1({pull_resistor_1_node_2[7], pull_resistor_1_node}), .out(multiplexer_1_out),
    .sel(and_5_out));
  Demultiplexer #(.select(2), .enable("false")) demultiplexer_1 (
    .out0(demultiplexer_1_out0), .out1(demultiplexer_1_out1), .out2(demultiplexer_1_out2),
    .out3(demultiplexer_1_out3), .in(1'b1), .sel(register_1_q[6:5]));
  Register register_1 (
    .D({pull_resistor_1_node_2[7], pull_resistor_1_node}), .en(demultiplexer_3_out1), .Q(register_1_q),
    .clk(Clock), .clr(Clear));
  Register register_2 (.D(multiplexer_2_out), .Q(register_2_q), .clk(Clock), .clr(Clear));  // open: en
  Multiplexer #(.width(8), .enable("false")) multiplexer_2 (
    .in0(adder_1_out), .in1({pull_resistor_1_node_2[7], pull_resistor_1_node}), .out(multiplexer_2_out),
    .sel(and_3_out));
  assign {pull_resistor_1_node_2[7], pull_resistor_1_node} = demultiplexer_4_out0 ? register_2_q : 8'bz;  // Controlled_Buffer controlled_buffer_2
  Demultiplexer #(.enable("false")) demultiplexer_2 (
    .out0(demultiplexer_2_out0), .out1(demultiplexer_2_out1), .in(demultiplexer_3_out3),
    .sel(pull_resistor_1_node_2[7]));
  and and_1 (and_1_out, demultiplexer_1_out2, nor_1_out);
  and and_2 (and_2_out, demultiplexer_1_out3, register_7_q[7]);
  Register #(.width(7)) register_3 (
    .D(pull_resistor_1_node), .en(demultiplexer_2_out0), .Q(register_3_q), .clk(Clock), .clr(Clear));
  Register register_4 (
    .D({pull_resistor_1_node_2[7], pull_resistor_1_node}), .en(demultiplexer_3_out4), .Q(register_4_q),
    .clk(Clock), .clr(Clear));
  Register register_5 (
    .D({pull_resistor_1_node_2[7], pull_resistor_1_node}), .en(demultiplexer_3_out5), .Q(register_5_q),
    .clk(Clock), .clr(Clear));
  assign not_1_out = ~register_5_q;  // NOT_Gate not_1, 8 bits wide
  Register register_6 (
    .D({pull_resistor_1_node_2[7], pull_resistor_1_node}), .en(demultiplexer_3_out6), .Q(register_6_q),
    .clk(Clock), .clr(Clear));
  Register register_7 (
    .D({pull_resistor_1_node_2[7], pull_resistor_1_node}), .en(demultiplexer_3_out7), .Q(register_7_q),
    .clk(Clock), .clr(Clear));
  or or_1 (or_1_out, demultiplexer_1_out0, demultiplexer_1_out1, and_1_out, and_2_out);
  and and_3 (and_3_out, or_1_out, demultiplexer_3_out0);
  and and_4 (and_4_out, Clock, External_Write);
  assign {pull_resistor_1_node_2[7], pull_resistor_1_node} = demultiplexer_4_out15 ? {1'b0, register_3_q} : 8'bz;  // Controlled_Buffer controlled_buffer_3
  assign controlled_buffer_4_out = demultiplexer_4_out10 ? register_4_q : 8'bz;  // Controlled_Buffer controlled_buffer_4
  assign controlled_buffer_4_out = demultiplexer_4_out13 ? {register_3_q, 1'b0} : 8'bz;  // Controlled_Buffer controlled_buffer_5
  assign controlled_buffer_4_out = demultiplexer_4_out9 ? register_4_q : 8'bz;  // Controlled_Buffer controlled_buffer_6
  assign controlled_buffer_7_out = demultiplexer_4_out9 ? register_5_q : 8'bz;  // Controlled_Buffer controlled_buffer_7
  assign controlled_buffer_7_out = demultiplexer_4_out10 ? not_1_out : 8'bz;  // Controlled_Buffer controlled_buffer_8
  assign controlled_buffer_7_out = demultiplexer_4_out13 ? 8'h2 : 8'bz;  // Controlled_Buffer controlled_buffer_9
  Register register_8 (
    .D({pull_resistor_1_node_2[7], pull_resistor_1_node}), .en(demultiplexer_2_out1), .Q(Mar), .clk(Clock),
    .clr(Clear));
  and and_5 (and_5_out, demultiplexer_1_out1, demultiplexer_3_out0);
  ROM #(.addrWidth(13)) rom_1 (.addr({register_1_q[4:0], register_2_q}), .data(rom_1_data));  // open: sel
  RAM #(.addrWidth(7)) ram_1 (
    .addr(register_3_q), .data(ram_1_data), .clk(and_4_out), .ld(or_3_out), .clr(Clear));  // open: sel
  assign ram_1_data = External_Write ? {pull_resistor_1_node_2[7], pull_resistor_1_node} : 8'bz;  // Controlled_Buffer controlled_buffer_10
  Adder adder_2 (
    .a(controlled_buffer_4_out), .b(controlled_buffer_7_out), .out(adder_2_out), .cin(demultiplexer_4_out10));  // open: cout
  assign and_6_out = register_4_q & register_5_q;  // AND_Gate and_6, 8 bits wide
  assign or_2_out = register_4_q | register_5_q;  // OR_Gate or_2, 8 bits wide
  Multiplexer #(.width(8), .enable("false")) multiplexer_3 (
    .in0(rom_1_data), .in1(ram_1_data), .out(multiplexer_3_out), .sel(register_1_q[7]));
  assign {pull_resistor_1_node_2[7], pull_resistor_1_node} = multiplexer_3_out[7] ? {4'b0000, multiplexer_3_out[3:0]} : 8'bz;  // Controlled_Buffer controlled_buffer_11
  assign {pull_resistor_1_node_2[7], pull_resistor_1_node} = demultiplexer_4_out2 ? ram_1_data : 8'bz;  // Controlled_Buffer controlled_buffer_12
  assign {pull_resistor_1_node_2[7], pull_resistor_1_node} = demultiplexer_4_out13 ? adder_2_out : 8'bz;  // Controlled_Buffer controlled_buffer_13
  assign {pull_resistor_1_node_2[7], pull_resistor_1_node} = demultiplexer_4_out10 ? adder_2_out : 8'bz;  // Controlled_Buffer controlled_buffer_14
  assign {pull_resistor_1_node_2[7], pull_resistor_1_node} = demultiplexer_4_out9 ? adder_2_out : 8'bz;  // Controlled_Buffer controlled_buffer_15
  assign {pull_resistor_1_node_2[7], pull_resistor_1_node} = demultiplexer_4_out11 ? and_6_out : 8'bz;  // Controlled_Buffer controlled_buffer_16
  assign {pull_resistor_1_node_2[7], pull_resistor_1_node} = demultiplexer_4_out14 ? {ram_1_data[3:0], ram_1_data[7:4]} : 8'bz;  // Controlled_Buffer controlled_buffer_17
  assign {pull_resistor_1_node_2[7], pull_resistor_1_node} = demultiplexer_4_out12 ? or_2_out : 8'bz;  // Controlled_Buffer controlled_buffer_18
  Controlled_Buffer #(.width(8)) controlled_buffer_19 (.in(register_4_q), .en(demultiplexer_4_out4));  // open: out
  assign {pull_resistor_1_node_2[7], pull_resistor_1_node} = demultiplexer_4_out5 ? not_1_out : 8'bz;  // Controlled_Buffer controlled_buffer_20
  assign {pull_resistor_1_node_2[7], pull_resistor_1_node} = demultiplexer_4_out6 ? {register_6_q[6:0], 1'b0} : 8'bz;  // Controlled_Buffer controlled_buffer_21
  assign {pull_resistor_1_node_2[7], pull_resistor_1_node} = demultiplexer_4_out7 ? {1'b0, register_6_q[7:1]} : 8'bz;  // Controlled_Buffer controlled_buffer_22
  assign {pull_resistor_1_node_2[7], pull_resistor_1_node} = demultiplexer_4_out8 ? {register_7_q[3:0], register_7_q[7:4]} : 8'bz;  // Controlled_Buffer controlled_buffer_23
  assign {pull_resistor_1_node_2[7], pull_resistor_1_node} = External_Read ? Data_In : 8'bz;  // Controlled_Buffer controlled_buffer_24
  assign Data_Out = External_Write ? {pull_resistor_1_node_2[7], pull_resistor_1_node} : 8'bz;  // Controlled_Buffer controlled_buffer_25
  nor nor_1 (nor_1_out, register_7_q[0], register_7_q[1], register_7_q[2], register_7_q[3], register_7_q[4], register_7_q[5], register_7_q[6], register_7_q[7]);
  Demultiplexer #(.select(3), .enable("false")) demultiplexer_3 (
    .out0(demultiplexer_3_out0), .out1(demultiplexer_3_out1), .out2(External_Write),
    .out3(demultiplexer_3_out3), .out4(demultiplexer_3_out4), .out5(demultiplexer_3_out5),
    .out6(demultiplexer_3_out6), .out7(demultiplexer_3_out7), .in(1'b1), .sel(multiplexer_3_out[6:4]));
  or or_3 (or_3_out, demultiplexer_4_out2, demultiplexer_4_out14);
  not not_2 (not_2_out, multiplexer_3_out[7]);
  Demultiplexer #(.select(4), .enable("false")) demultiplexer_4 (
    .out0(demultiplexer_4_out0), .out1(demultiplexer_4_out1), .out2(demultiplexer_4_out2),
    .out3(External_Read), .out4(demultiplexer_4_out4), .out5(demultiplexer_4_out5),
    .out6(demultiplexer_4_out6), .out7(demultiplexer_4_out7), .out8(demultiplexer_4_out8),
    .out9(demultiplexer_4_out9), .out10(demultiplexer_4_out10), .out11(demultiplexer_4_out11),
    .out12(demultiplexer_4_out12), .out13(demultiplexer_4_out13), .out14(demultiplexer_4_out14),
    .out15(demultiplexer_4_out15), .in(not_2_out), .sel(multiplexer_3_out[3:0]));
endmodule
