// Logisim project Advanced Processor 2.circ as structural Verilog: 1 circuit, main circuit main
module main (
  input  in_1
);

  wire and_1_out, and_2_out, and_3_out, and_4_out, and_6_out, clock_1_out, demultiplexer_1_out0,
       demultiplexer_1_out1, demultiplexer_1_out2, demultiplexer_1_out3, demultiplexer_2_out0,
       demultiplexer_2_out1, demultiplexer_2_out2, demultiplexer_2_out3, demultiplexer_2_out4,
       demultiplexer_2_out5, demultiplexer_2_out6, demultiplexer_2_out7, demultiplexer_3_out0,
       demultiplexer_3_out1, demultiplexer_3_out2, demultiplexer_3_out3, demultiplexer_3_out4,
       demultiplexer_3_out5, demultiplexer_3_out6, demultiplexer_3_out7, demultiplexer_3_out8,
       demultiplexer_3_out9, demultiplexer_3_out10, demultiplexer_3_out11, demultiplexer_3_out12,
       demultiplexer_3_out13, demultiplexer_3_out14, demultiplexer_3_out15, nor_1_out, not_2_out, or_1_out,
       or_3_out;
  wire [7:0] adder_1_out, adder_2_out, and_7_out, controlled_buffer_4_out, controlled_buffer_7_out,
       controlled_buffer_25_out, multiplexer_1_out, multiplexer_2_out, multiplexer_3_out, not_1_out,
       or_2_out, pull_resistor_1_node, ram_1_data, register_1_q, register_2_q, register_3_q, register_4_q,
       register_5_q, register_6_q, register_7_q, rom_1_data, undriven;

  Pull_Resistor pull_resistor_1 (.node(pull_resistor_1_node));
  Clock clock_1 (.out(clock_1_out));
  assign pull_resistor_1_node = demultiplexer_3_out1 ? register_1_q : 8'bz;  // Controlled_Buffer controlled_buffer_1
  Adder adder_1 (.a(register_2_q), .b(multiplexer_1_out), .out(adder_1_out));  // open: cin, cout
  Multiplexer #(.width(8), .enable("false")) multiplexer_1 (
    .in0(8'h1), .in1(pull_resistor_1_node), .out(multiplexer_1_out), .sel(and_6_out));
  Demultiplexer #(.select(2), .enable("false")) demultiplexer_1 (
    .out0(demultiplexer_1_out0), .out1(demultiplexer_1_out1), .out2(demultiplexer_1_out2),
    .out3(demultiplexer_1_out3), .in(1'b1), .sel(register_1_q[6:5]));
  Register register_1 (
    .D(pull_resistor_1_node), .en(demultiplexer_2_out1), .Q(register_1_q), .clk(clock_1_out), .clr(in_1));
  Register register_2 (.D(multiplexer_2_out), .Q(register_2_q), .clk(clock_1_out), .clr(in_1));  // open: en
  Multiplexer #(.width(8), .enable("false")) multiplexer_2 (
    .in0(adder_1_out), .in1(pull_resistor_1_node), .out(multiplexer_2_out), .sel(and_3_out));
  assign pull_resistor_1_node = demultiplexer_3_out0 ? register_2_q : 8'bz;  // Controlled_Buffer controlled_buffer_2
  and and_1 (and_1_out, demultiplexer_1_out2, nor_1_out);
  and and_2 (and_2_out, demultiplexer_1_out3, register_7_q[7]);
  Register register_3 (
    .D(pull_resistor_1_node), .en(demultiplexer_2_out3), .Q(register_3_q), .clk(clock_1_out), .clr(in_1));
  Register register_4 (
    .D(pull_resistor_1_node), .en(demultiplexer_2_out4), .Q(register_4_q), .clk(clock_1_out), .clr(in_1));
  Register register_5 (
    .D(pull_resistor_1_node), .en(demultiplexer_2_out5), .Q(register_5_q), .clk(clock_1_out), .clr(in_1));
  assign not_1_out = ~register_5_q;  // NOT_Gate not_1, 8 bits wide
  Register register_6 (
    .D(pull_resistor_1_node), .en(demultiplexer_2_out6), .Q(register_6_q), .clk(clock_1_out), .clr(in_1));
  Register register_7 (
    .D(pull_resistor_1_node), .en(demultiplexer_2_out7), .Q(register_7_q), .clk(clock_1_out), .clr(in_1));
  or or_1 (or_1_out, demultiplexer_1_out0, demultiplexer_1_out1, and_1_out, and_2_out);
  and and_3 (and_3_out, or_1_out, demultiplexer_2_out0);
  and and_4 (and_4_out, clock_1_out, demultiplexer_2_out2);
  assign pull_resistor_1_node = demultiplexer_3_out15 ? undriven : 8'bz;  // Controlled_Buffer controlled_buffer_3
  assign controlled_buffer_4_out = demultiplexer_3_out10 ? register_4_q : 8'bz;  // Controlled_Buffer controlled_buffer_4
  assign controlled_buffer_4_out = demultiplexer_3_out13 ? {undriven[6:0], 1'b0} : 8'bz;  // Controlled_Buffer controlled_buffer_5
  assign controlled_buffer_4_out = demultiplexer_3_out9 ? register_4_q : 8'bz;  // Controlled_Buffer controlled_buffer_6
  assign controlled_buffer_7_out = demultiplexer_3_out9 ? register_5_q : 8'bz;  // Controlled_Buffer controlled_buffer_7
  assign controlled_buffer_7_out = demultiplexer_3_out10 ? not_1_out : 8'bz;  // Controlled_Buffer controlled_buffer_8
  assign controlled_buffer_7_out = demultiplexer_3_out13 ? 8'h2 : 8'bz;  // Controlled_Buffer controlled_buffer_9
  // AND_Gate and_5 has open pins: in0=clock_1_out, in1=demultiplexer_2_out2, out=open
  and and_6 (and_6_out, demultiplexer_1_out1, demultiplexer_2_out0);
  ROM #(.addrWidth(13)) rom_1 (.addr({register_1_q[4:0], register_2_q}), .data(rom_1_data));  // open: sel
  RAM ram_1 (.addr(register_3_q), .data(ram_1_data), .clk(and_4_out), .ld(or_3_out), .clr(in_1));  // open: sel
  assign ram_1_data = demultiplexer_2_out2 ? pull_resistor_1_node : 8'bz;  // Controlled_Buffer controlled_buffer_10
  Adder adder_2 (
    .a(controlled_buffer_4_out), .b(controlled_buffer_7_out), .out(adder_2_out), .cin(demultiplexer_3_out10));  // open: cout
  assign and_7_out = register_4_q & register_5_q;  // AND_Gate and_7, 8 bits wide
  assign or_2_out = register_4_q | register_5_q;  // OR_Gate or_2, 8 bits wide
  assign pull_resistor_1_node = demultiplexer_3_out3 ? controlled_buffer_25_out : 8'bz;  // Controlled_Buffer controlled_buffer_11
  Multiplexer #(.width(8), .enable("false")) multiplexer_3 (
    .in0(rom_1_data), .in1(ram_1_data), .out(multiplexer_3_out), .sel(register_1_q[7]));
  assign pull_resistor_1_node = multiplexer_3_out[7] ? {4'b0000, multiplexer_3_out[3:0]} : 8'bz;  // Controlled_Buffer controlled_buffer_12
  assign pull_resistor_1_node = demultiplexer_3_out2 ? ram_1_data : 8'bz;  // Controlled_Buffer controlled_buffer_13
  assign pull_resistor_1_node = demultiplexer_3_out13 ? adder_2_out : 8'bz;  // Controlled_Buffer controlled_buffer_14
  assign pull_resistor_1_node = demultiplexer_3_out10 ? adder_2_out : 8'bz;  // Controlled_Buffer controlled_buffer_15
  assign pull_resistor_1_node = demultiplexer_3_out9 ? adder_2_out : 8'bz;  // Controlled_Buffer controlled_buffer_16
  assign pull_resistor_1_node = demultiplexer_3_out11 ? and_7_out : 8'bz;  // Controlled_Buffer controlled_buffer_17
  assign pull_resistor_1_node = demultiplexer_3_out14 ? {ram_1_data[3:0], ram_1_data[7:4]} : 8'bz;  // Controlled_Buffer controlled_buffer_18
  assign pull_resistor_1_node = demultiplexer_3_out12 ? or_2_out : 8'bz;  // Controlled_Buffer controlled_buffer_19
  assign pull_resistor_1_node = demultiplexer_3_out4 ? register_4_q : 8'bz;  // Controlled_Buffer controlled_buffer_20
  assign pull_resistor_1_node = demultiplexer_3_out5 ? not_1_out : 8'bz;  // Controlled_Buffer controlled_buffer_21
  assign pull_resistor_1_node = demultiplexer_3_out6 ? {register_6_q[6:0], 1'b0} : 8'bz;  // Controlled_Buffer controlled_buffer_22
  assign pull_resistor_1_node = demultiplexer_3_out7 ? {1'b0, register_6_q[7:1]} : 8'bz;  // Controlled_Buffer controlled_buffer_23
  assign pull_resistor_1_node = demultiplexer_3_out8 ? {register_7_q[3:0], register_7_q[7:4]} : 8'bz;  // Controlled_Buffer controlled_buffer_24
  assign controlled_buffer_25_out = demultiplexer_2_out2 ? pull_resistor_1_node : 8'bz;  // Controlled_Buffer controlled_buffer_25
  nor nor_1 (nor_1_out, register_7_q[0], register_7_q[1], register_7_q[2], register_7_q[3], register_7_q[4], register_7_q[5], register_7_q[6], register_7_q[7]);
  Demultiplexer #(.select(3), .enable("false")) demultiplexer_2 (
    .out0(demultiplexer_2_out0), .out1(demultiplexer_2_out1), .out2(demultiplexer_2_out2),
    .out3(demultiplexer_2_out3), .out4(demultiplexer_2_out4), .out5(demultiplexer_2_out5),
    .out6(demultiplexer_2_out6), .out7(demultiplexer_2_out7), .in(1'b1), .sel(multiplexer_3_out[6:4]));
  or or_3 (or_3_out, demultiplexer_3_out2, demultiplexer_3_out14);
  not not_2 (not_2_out, multiplexer_3_out[7]);
  Demultiplexer #(.select(4), .enable("false")) demultiplexer_3 (
    .out0(demultiplexer_3_out0), .out1(demultiplexer_3_out1), .out2(demultiplexer_3_out2),
    .out3(demultiplexer_3_out3), .out4(demultiplexer_3_out4), .out5(demultiplexer_3_out5),
    .out6(demultiplexer_3_out6), .out7(demultiplexer_3_out7), .out8(demultiplexer_3_out8),
    .out9(demultiplexer_3_out9), .out10(demultiplexer_3_out10), .out11(demultiplexer_3_out11),
    .out12(demultiplexer_3_out12), .out13(demultiplexer_3_out13), .out14(demultiplexer_3_out14),
    .out15(demultiplexer_3_out15), .in(not_2_out), .sel(multiplexer_3_out[3:0]));

  // Notes on the sheet:
  //   contents of rom_1 (hex, n*v repeats v):
  //   82 81 f4 8 9*44 82 44 48 d0 55 f4 18 49 a2 74 7 40 d8 90 78 55 9 44 48 d0 55 f4 18 49 a2 74 7 40 d8
  //   90 78 55 9 44 48 d0 55 f4 18 49 a2 74 7 40 d8 90 78 55 9 44 44 40 de 69 66 b4 f0 48 d1 49 f1 8 44 44
  //   44 90 44 40 de 69 66 b0 f0 48 d1 49 f2 8 44 44 44 90 44 81
endmodule
