// Logisim project BIOSBOOTDEMO.circ as structural Verilog: 1 circuit, main circuit main
module main (
  input  in_1,
  input  in_2,
  input  in_3,
  input  in_4,
  input  in_5,
  input  in_6,
  input  in_7,
  output [7:0] out_8
);

  wire not_1_out, or_1_out;
  wire [7:0] adder_1_out, adder_2_out, controlled_buffer_2_out, multiplexer_1_out, multiplexer_2_out,
       ram_1_data, register_1_q, register_2_q;

  Multiplexer #(.width(8)) multiplexer_1 (
    .in0(adder_1_out), .in1(ram_1_data), .out(multiplexer_1_out), .sel(in_5));  // open: en
  Register register_1 (.D(multiplexer_1_out), .Q(register_1_q), .clk(in_1), .clr(in_7));  // open: en
  Adder adder_1 (.a(register_1_q), .b(8'h1), .out(adder_1_out));  // open: cin, cout
  or or_1 (or_1_out, in_2, in_3);
  RAM ram_1 (.addr(register_1_q), .data(ram_1_data), .sel(or_1_out), .clk(in_1), .ld(in_3), .clr(in_7));
  Multiplexer #(.width(8)) multiplexer_2 (
    .in0(adder_2_out), .in1(ram_1_data), .out(multiplexer_2_out), .sel(in_6));  // open: en
  Register register_2 (.D(multiplexer_2_out), .Q(register_2_q), .clk(in_1), .clr(in_7));  // open: en
  Adder adder_2 (.a(register_2_q), .b(8'h1), .out(adder_2_out));  // open: cin, cout
  ROM rom_1 (.addr(register_2_q), .data(out_8), .sel(in_4));
  assign ram_1_data = not_1_out ? out_8 : 8'bz;  // Controlled_Buffer controlled_buffer_1
  not not_1 (not_1_out, out_8[7]);
  assign controlled_buffer_2_out = out_8[7] ? out_8 : 8'bz;  // Controlled_Buffer controlled_buffer_2

  // Notes on the sheet:
  //   Inherent Decoder
endmodule
