// Logisim project Coms Processor 1.circ as structural Verilog: 1 circuit, main circuit main
module main (
  input  in_1
);

  wire clock_1_out, demultiplexer_1_out0, demultiplexer_1_out1, demultiplexer_1_out2, demultiplexer_1_out3,
       demultiplexer_1_out4, demultiplexer_1_out5, demultiplexer_1_out6, demultiplexer_1_out7,
       demultiplexer_1_out8, demultiplexer_1_out9, demultiplexer_1_out10, demultiplexer_1_out11,
       demultiplexer_1_out12, demultiplexer_1_out13, demultiplexer_1_out14, demultiplexer_1_out15,
       demultiplexer_2_out0, demultiplexer_2_out1, demultiplexer_2_out2, demultiplexer_2_out3,
       demultiplexer_2_out4, demultiplexer_2_out5, demultiplexer_2_out6, demultiplexer_2_out7,
       demultiplexer_2_out8, demultiplexer_2_out9, demultiplexer_2_out10, demultiplexer_2_out11,
       demultiplexer_2_out12, demultiplexer_2_out13, demultiplexer_2_out14, demultiplexer_2_out15,
       j_k_ff_1_q, j_k_ff_2_q, j_k_ff_2_qn, or_1_out, or_2_out, or_3_out, or_4_out;
  wire [7:0] adder_1_out, adder_2_out, and_1_out, multiplexer_1_out, multiplexer_2_out, multiplexer_3_out,
       not_1_out, or_5_out, pull_resistor_1_node, ram_1_data, register_1_q, register_2_q, register_3_q,
       register_4_q, register_5_q, register_6_q, register_7_q, register_8_q, register_9_q, register_10_q,
       register_11_q, register_12_q, rom_1_data;

  Pull_Resistor pull_resistor_1 (.node(pull_resistor_1_node));
  or or_1 (or_1_out, demultiplexer_1_out2, demultiplexer_2_out1);
  assign pull_resistor_1_node = demultiplexer_2_out3 ? register_9_q : 8'bz;  // Controlled_Buffer controlled_buffer_1
  Register register_1 (
    .D(pull_resistor_1_node), .en(demultiplexer_1_out1), .Q(register_1_q), .clk(clock_1_out), .clr(in_1));
  Adder adder_1 (.a(register_2_q), .b(8'h1), .out(adder_1_out));  // open: cin, cout
  Multiplexer #(.width(8), .enable("false")) multiplexer_1 (
    .in0(adder_1_out), .in1(pull_resistor_1_node), .out(multiplexer_1_out), .sel(demultiplexer_1_out0));
  Register register_2 (.D(multiplexer_1_out), .Q(register_2_q), .clk(clock_1_out), .clr(in_1));  // open: en
  assign pull_resistor_1_node = demultiplexer_2_out0 ? register_2_q : 8'bz;  // Controlled_Buffer controlled_buffer_2
  assign pull_resistor_1_node = demultiplexer_2_out1 ? register_1_q : 8'bz;  // Controlled_Buffer controlled_buffer_3
  or or_2 (or_2_out, demultiplexer_2_out5, demultiplexer_2_out9);
  Register register_3 (
    .D(pull_resistor_1_node), .en(demultiplexer_1_out4), .Q(register_3_q), .clk(clock_1_out), .clr(in_1));
  Register register_4 (
    .D(pull_resistor_1_node), .en(demultiplexer_1_out5), .Q(register_4_q), .clk(clock_1_out), .clr(in_1));
  assign not_1_out = ~register_4_q;  // NOT_Gate not_1, 8 bits wide
  Register register_5 (
    .D(pull_resistor_1_node), .en(demultiplexer_1_out6), .Q(register_5_q), .clk(clock_1_out), .clr(in_1));
  Register register_6 (
    .D(pull_resistor_1_node), .en(demultiplexer_1_out7), .Q(register_6_q), .clk(clock_1_out), .clr(in_1));
  Register register_7 (
    .D(pull_resistor_1_node), .en(demultiplexer_1_out12), .Q(register_7_q), .clk(clock_1_out), .clr(in_1));
  Register register_8 (
    .D(pull_resistor_1_node), .en(demultiplexer_1_out13), .Q(register_8_q), .clk(clock_1_out), .clr(in_1));
  Register register_9 (
    .D(pull_resistor_1_node), .en(demultiplexer_1_out3), .Q(register_9_q), .clk(clock_1_out), .clr(in_1));
  assign pull_resistor_1_node = demultiplexer_2_out4 ? register_3_q : 8'bz;  // Controlled_Buffer controlled_buffer_4
  Multiplexer #(.width(8), .enable("false")) multiplexer_2 (
    .in0(register_4_q), .in1(not_1_out), .out(multiplexer_2_out), .sel(or_2_out));
  assign pull_resistor_1_node = demultiplexer_2_out5 ? multiplexer_2_out : 8'bz;  // Controlled_Buffer controlled_buffer_5
  assign pull_resistor_1_node = demultiplexer_2_out6 ? register_5_q : 8'bz;  // Controlled_Buffer controlled_buffer_6
  assign pull_resistor_1_node = demultiplexer_2_out7 ? register_6_q : 8'bz;  // Controlled_Buffer controlled_buffer_7
  assign pull_resistor_1_node = demultiplexer_2_out12 ? register_7_q : 8'bz;  // Controlled_Buffer controlled_buffer_8
  assign pull_resistor_1_node = demultiplexer_2_out13 ? register_8_q : 8'bz;  // Controlled_Buffer controlled_buffer_9
  J_K_Flip_Flop j_k_ff_1 (
    .J(demultiplexer_1_out8), .clk(clock_1_out), .K(j_k_ff_1_q), .Q(j_k_ff_1_q), .reset(in_1));  // open: Qn, preset, en
  ROM #(.addrWidth(16)) rom_1 (.addr({register_1_q, register_2_q}), .data(rom_1_data));  // open: sel
  Multiplexer #(.width(8), .enable("false")) multiplexer_3 (
    .in0(rom_1_data), .in1(ram_1_data), .out(multiplexer_3_out), .sel(j_k_ff_1_q));
  assign pull_resistor_1_node = demultiplexer_2_out2 ? ram_1_data : 8'bz;  // Controlled_Buffer controlled_buffer_10
  RAM ram_1 (
    .addr(register_9_q), .data(ram_1_data), .sel(or_1_out), .clk(clock_1_out), .ld(demultiplexer_2_out2),
    .clr(in_1));
  assign ram_1_data = demultiplexer_1_out2 ? pull_resistor_1_node : 8'bz;  // Controlled_Buffer controlled_buffer_11
  J_K_Flip_Flop j_k_ff_2 (
    .J(demultiplexer_1_out9), .clk(clock_1_out), .K(j_k_ff_2_q), .Q(j_k_ff_2_q), .Qn(j_k_ff_2_qn),
    .reset(in_1));  // open: preset, en
  Register register_10 (.D(multiplexer_3_out), .en(j_k_ff_2_qn), .Q(register_10_q), .clk(clock_1_out), .clr(in_1));
  assign pull_resistor_1_node = j_k_ff_2_q ? multiplexer_3_out : 8'bz;  // Controlled_Buffer controlled_buffer_12
  or or_3 (or_3_out, demultiplexer_2_out8, demultiplexer_2_out9);
  or or_4 (or_4_out, demultiplexer_2_out8, demultiplexer_2_out9);
  Adder adder_2 (.a(register_3_q), .b(multiplexer_2_out), .out(adder_2_out), .cin(or_3_out));  // open: cout
  assign pull_resistor_1_node = or_4_out ? adder_2_out : 8'bz;  // Controlled_Buffer controlled_buffer_13
  assign and_1_out = register_3_q & multiplexer_2_out;  // AND_Gate and_1, 8 bits wide
  assign pull_resistor_1_node = demultiplexer_2_out10 ? and_1_out : 8'bz;  // Controlled_Buffer controlled_buffer_14
  assign or_5_out = register_3_q | multiplexer_2_out;  // OR_Gate or_5, 8 bits wide
  Demultiplexer #(.select(4), .enable("false")) demultiplexer_1 (
    .out0(demultiplexer_1_out0), .out1(demultiplexer_1_out1), .out2(demultiplexer_1_out2),
    .out3(demultiplexer_1_out3), .out4(demultiplexer_1_out4), .out5(demultiplexer_1_out5),
    .out6(demultiplexer_1_out6), .out7(demultiplexer_1_out7), .out8(demultiplexer_1_out8),
    .out9(demultiplexer_1_out9), .out10(demultiplexer_1_out10), .out11(demultiplexer_1_out11),
    .out12(demultiplexer_1_out12), .out13(demultiplexer_1_out13), .out14(demultiplexer_1_out14),
    .out15(demultiplexer_1_out15), .in(1'b1), .sel(register_10_q[7:4]));
  assign pull_resistor_1_node = demultiplexer_2_out11 ? or_5_out : 8'bz;  // Controlled_Buffer controlled_buffer_15
  Register register_11 (
    .D(pull_resistor_1_node), .en(demultiplexer_1_out14), .Q(register_11_q), .clk(clock_1_out), .clr(in_1));
  assign pull_resistor_1_node = demultiplexer_2_out14 ? register_11_q : 8'bz;  // Controlled_Buffer controlled_buffer_16
  assign pull_resistor_1_node = demultiplexer_2_out15 ? register_12_q : 8'bz;  // Controlled_Buffer controlled_buffer_17
  Register register_12 (
    .D(pull_resistor_1_node), .en(demultiplexer_1_out15), .Q(register_12_q), .clk(clock_1_out), .clr(in_1));
  Demultiplexer #(.select(4), .enable("false")) demultiplexer_2 (
    .out0(demultiplexer_2_out0), .out1(demultiplexer_2_out1), .out2(demultiplexer_2_out2),
    .out3(demultiplexer_2_out3), .out4(demultiplexer_2_out4), .out5(demultiplexer_2_out5),
    .out6(demultiplexer_2_out6), .out7(demultiplexer_2_out7), .out8(demultiplexer_2_out8),
    .out9(demultiplexer_2_out9), .out10(demultiplexer_2_out10), .out11(demultiplexer_2_out11),
    .out12(demultiplexer_2_out12), .out13(demultiplexer_2_out13), .out14(demultiplexer_2_out14),
    .out15(demultiplexer_2_out15), .in(j_k_ff_2_qn), .sel(register_10_q[3:0]));
  Clock clock_1 (.out(clock_1_out));
endmodule
