// Logisim project balls.circ as structural Verilog: 1 circuit, main circuit main
module main (
);

  wire [7:0] Controls_Register_q;

  Register Controls_Register (.Q(Controls_Register_q));  // open: D, en, clk, clr
  Counter counter_1 ();  // open: load, D, count, Q, carry, clk, clr
endmodule
