// Logisim project h.circ as structural Verilog: 1 circuit, main circuit main
module main (
  input  in_1,
  input  [7:0] in_2,
  input  [2:0] in_3
);

  wire clock_1_out, not_1_out;
  wire [2:0] counter_1_q, multiplexer_1_out;
  wire [7:0] controlled_buffer_1_out, controlled_buffer_2_out, demultiplexer_1_out0, demultiplexer_1_out1,
       demultiplexer_1_out2, demultiplexer_1_out3, demultiplexer_1_out4, demultiplexer_1_out5,
       demultiplexer_1_out6, demultiplexer_1_out7;

  Counter #(.width(3), .max('h7)) counter_1 (.Q(counter_1_q), .clk(clock_1_out));  // open: load, D, count, carry, clr
  Clock clock_1 (.out(clock_1_out));
  Multiplexer #(.width(3), .enable("false")) multiplexer_1 (
    .in0(counter_1_q), .in1(in_3), .out(multiplexer_1_out), .sel(in_1));
  assign controlled_buffer_1_out = in_1 ? in_2 : 8'bz;  // Controlled_Buffer controlled_buffer_1
  RAM #(.addrWidth(3)) ram_1 (
    .addr(multiplexer_1_out), .data(controlled_buffer_1_out), .clk(clock_1_out), .ld(not_1_out));  // open: sel, clr
  DotMatrix #(.inputtype("row"), .matrixcols(8), .matrixrows(8), .persist(1)) dotmatrix_1 (
    .row0(demultiplexer_1_out0), .row1(demultiplexer_1_out1), .row2(demultiplexer_1_out2),
    .row3(demultiplexer_1_out3), .row4(demultiplexer_1_out4), .row5(demultiplexer_1_out5),
    .row6(demultiplexer_1_out6), .row7(demultiplexer_1_out7));
  not not_1 (not_1_out, in_1);
  assign controlled_buffer_2_out = not_1_out ? controlled_buffer_1_out : 8'bz;  // Controlled_Buffer controlled_buffer_2
  Demultiplexer #(.select(3), .width(8), .enable("false")) demultiplexer_1 (
    .out0(demultiplexer_1_out0), .out1(demultiplexer_1_out1), .out2(demultiplexer_1_out2),
    .out3(demultiplexer_1_out3), .out4(demultiplexer_1_out4), .out5(demultiplexer_1_out5),
    .out6(demultiplexer_1_out6), .out7(demultiplexer_1_out7), .in(controlled_buffer_2_out), .sel(counter_1_q));
endmodule
