// Logisim project ram design.circ as structural Verilog: 6 circuits, main circuit main
module main (
  input  MAR0,
  input  MAR1,
  input  MAR2,
  input  MAR3,
  input  MAR4,
  input  MAR5,
  input  MAR6,
  input  MAR7,
  input  CLR,
  input  CLK,
  input  RQST,
  input  SEND,
  input  DATA0,
  input  DATA1,
  input  DATA2,
  input  DATA3,
  input  DATA4,
  input  DATA5,
  input  DATA6,
  input  DATA7,
  output out_21,
  output out_22,
  output out_23,
  output out_24,
  output out_25,
  output out_26,
  output out_27,
  output out_28
);

  wire and_1_out, and_2_out, n74ls138_1_y0, n74ls138_1_y1, n74ls138_1_y2, n74ls138_1_y3, n74ls138_1_y5,
       n74ls138_1_y6, n74ls163_1_qa, n74ls163_1_qb, n74ls163_1_qc, n74ls163_1_qd, n74ls273_1__1q,
       n74ls273_1__2q, n74ls273_1__3q, n74ls273_1__4q, n74ls273_1__5q, n74ls273_1__6q, n74ls273_1__7q,
       n74ls273_1__8q, not_1_out;

  not not_1 (not_1_out, SEND);
  assign out_21 = not_1_out ? DATA0 : 1'bz;  // Controlled_Buffer controlled_buffer_1
  assign out_22 = not_1_out ? DATA1 : 1'bz;  // Controlled_Buffer controlled_buffer_2
  assign out_23 = not_1_out ? DATA2 : 1'bz;  // Controlled_Buffer controlled_buffer_3
  assign out_24 = not_1_out ? DATA3 : 1'bz;  // Controlled_Buffer controlled_buffer_4
  assign out_25 = not_1_out ? DATA4 : 1'bz;  // Controlled_Buffer controlled_buffer_5
  assign out_26 = not_1_out ? DATA5 : 1'bz;  // Controlled_Buffer controlled_buffer_6
  assign out_27 = not_1_out ? DATA6 : 1'bz;  // Controlled_Buffer controlled_buffer_7
  assign out_28 = not_1_out ? DATA7 : 1'bz;  // Controlled_Buffer controlled_buffer_8
  _74ls138 u_74ls138_1 (
    .A(SEND), .B(MAR4), .C(MAR5), .G2A(MAR6), .G2B(MAR7), .G1(1'b1), .Y0(n74ls138_1_y0), .Y1(n74ls138_1_y1),
    .Y2(n74ls138_1_y2), .Y3(n74ls138_1_y3), .Y5(n74ls138_1_y5), .Y6(n74ls138_1_y6));  // open: Y4, Y7
  _74ls273 u_74ls273_1 (
    .CLR(CLR), ._1D(out_21), ._2D(out_22), ._3D(out_23), ._4D(out_24), ._5D(out_25), ._6D(out_26),
    ._7D(out_27), ._8D(out_28), .CLK(n74ls138_1_y5), ._1Q(n74ls273_1__1q), ._2Q(n74ls273_1__2q),
    ._3Q(n74ls273_1__3q), ._4Q(n74ls273_1__4q), ._5Q(n74ls273_1__5q), ._6Q(n74ls273_1__6q),
    ._7Q(n74ls273_1__7q), ._8Q(n74ls273_1__8q));
  _74ls163 u_74ls163_1 (
    .CLR(CLR), .CLK(SEND), .A(out_21), .B(out_22), .C(out_23), .D(out_24), .LOAD(n74ls138_1_y6), .ENT(MAR0),
    .ENP(MAR0), .QA(n74ls163_1_qa), .QB(n74ls163_1_qb), .QC(n74ls163_1_qc), .QD(n74ls163_1_qd));  // open: RCO
  HM62256 hm62256_1 (
    .A0(n74ls163_1_qa), .A1(n74ls163_1_qb), .A2(n74ls163_1_qc), .A3(n74ls163_1_qd), .A4(n74ls273_1__5q),
    .A5(n74ls273_1__6q), .A6(n74ls273_1__7q), .A7(n74ls273_1__8q), .A8(n74ls273_1__1q), .A9(n74ls273_1__2q),
    .A10(n74ls273_1__3q), .A11(n74ls273_1__4q), .A12(MAR1), .d0(out_21), .A13(MAR2), .d1(out_22), .A14(MAR3),
    .d2(out_23), .d3(out_24), .d4(out_25), .d5(out_26), .d6(out_27), .WE(n74ls138_1_y0), .d7(out_28),
    .OE(n74ls138_1_y1), .CS(and_1_out), .q0(out_21), .q1(out_22), .q2(out_23), .q3(out_24), .q4(out_25),
    .q5(out_26), .q6(out_27), .q7(out_28));
  HM62256 hm62256_2 (
    .A0(n74ls163_1_qa), .A1(n74ls163_1_qb), .A2(n74ls163_1_qc), .A3(n74ls163_1_qd), .A4(n74ls273_1__5q),
    .A5(n74ls273_1__6q), .A6(n74ls273_1__7q), .A7(n74ls273_1__8q), .A8(n74ls273_1__1q), .A9(n74ls273_1__2q),
    .A10(n74ls273_1__3q), .A11(n74ls273_1__4q), .A12(MAR1), .d0(out_21), .A13(MAR2), .d1(out_22), .A14(MAR3),
    .d2(out_23), .d3(out_24), .d4(out_25), .d5(out_26), .d6(out_27), .WE(n74ls138_1_y2), .d7(out_28),
    .OE(n74ls138_1_y3), .CS(and_2_out), .q0(out_21), .q1(out_22), .q2(out_23), .q3(out_24), .q4(out_25),
    .q5(out_26), .q6(out_27), .q7(out_28));
  and and_1 (and_1_out, n74ls138_1_y1, n74ls138_1_y0);
  and and_2 (and_2_out, n74ls138_1_y3, n74ls138_1_y2);
endmodule

module _74ls138 (
  input  A,
  input  B,
  input  C,
  input  G2A,
  input  G2B,
  input  G1,
  output Y0,
  output Y1,
  output Y2,
  output Y3,
  output Y4,
  output Y5,
  output Y6,
  output Y7
);

  wire and_1_out, decoder_1_out0, decoder_1_out1, decoder_1_out2, decoder_1_out3, decoder_1_out4,
       decoder_1_out5, decoder_1_out6, decoder_1_out7;

  and and_1 (and_1_out, ~G2A, ~G2B, G1);  // AND_Gate
  not not_1 (Y0, decoder_1_out0);
  not not_2 (Y1, decoder_1_out1);
  not not_3 (Y2, decoder_1_out2);
  not not_4 (Y3, decoder_1_out3);
  not not_5 (Y4, decoder_1_out4);
  not not_6 (Y5, decoder_1_out5);
  not not_7 (Y6, decoder_1_out6);
  not not_8 (Y7, decoder_1_out7);
  Decoder #(.select(3), .disabled(0)) decoder_1 (
    .out0(decoder_1_out0), .out1(decoder_1_out1), .out2(decoder_1_out2), .out3(decoder_1_out3),
    .out4(decoder_1_out4), .out5(decoder_1_out5), .out6(decoder_1_out6), .out7(decoder_1_out7),
    .sel({C, B, A}), .en(and_1_out));
endmodule

module _74ls163 (
  input  CLR,
  input  CLK,
  input  A,
  input  B,
  input  C,
  input  D,
  input  LOAD,
  input  ENT,
  input  ENP,
  output RCO,
  output QA,
  output QB,
  output QC,
  output QD
);

  wire and_1_out, not_1_out, not_2_out;

  not not_1 (not_1_out, CLR);
  not not_2 (not_2_out, LOAD);
  and and_1 (and_1_out, ENT, ENP);
  Counter #(.width(4), .max('hf)) counter_1 (
    .load(not_2_out), .D({D, C, B, A}), .count(and_1_out), .Q({QD, QC, QB, QA}), .carry(RCO), .clk(CLK),
    .clr(not_1_out));
endmodule

module _74ls273 (
  input  CLR,
  input  _1D,
  input  _2D,
  input  _3D,
  input  _4D,
  input  _5D,
  input  _6D,
  input  _7D,
  input  _8D,
  input  CLK,
  output _1Q,
  output _2Q,
  output _3Q,
  output _4Q,
  output _5Q,
  output _6Q,
  output _7Q,
  output _8Q
);

  wire not_1_out;

  not not_1 (not_1_out, CLR);
  Register register_1 (
    .D({_8D, _7D, _6D, _5D, _4D, _3D, _2D, _1D}), .en(1'b1), .Q({_8Q, _7Q, _6Q, _5Q, _4Q, _3Q, _2Q, _1Q}),
    .clk(CLK), .clr(not_1_out));
endmodule

module HM62256 (
  input  A0,
  input  A1,
  input  A2,
  input  A3,
  input  A4,
  input  A5,
  input  A6,
  input  A7,
  input  A8,
  input  A9,
  input  A10,
  input  A11,
  input  A12,
  input  d0,
  input  A13,
  input  d1,
  input  A14,
  input  d2,
  input  d3,
  input  d4,
  input  d5,
  input  d6,
  input  WE,
  input  d7,
  input  OE,
  input  CS,
  output q0,
  output q1,
  output q2,
  output q3,
  output q4,
  output q5,
  output q6,
  output q7
);

  wire not_1_out, not_2_out, not_3_out;
  wire [7:0] ram_1_data;

  not not_1 (not_1_out, WE);
  not not_2 (not_2_out, OE);
  not not_3 (not_3_out, CS);
  RAM #(.addrWidth(15)) ram_1 (
    .addr({A14, A13, A12, A11, A10, A9, A8, A7, A6, A5, A4, A3, A2, A1, A0}), .data(ram_1_data),
    .sel(not_3_out), .clk(WE), .ld(not_2_out), .clr(1'b0));
  assign ram_1_data[0] = not_1_out ? d0 : 1'bz;  // Controlled_Buffer controlled_buffer_1
  assign ram_1_data[1] = not_1_out ? d1 : 1'bz;  // Controlled_Buffer controlled_buffer_2
  assign ram_1_data[2] = not_1_out ? d2 : 1'bz;  // Controlled_Buffer controlled_buffer_3
  assign ram_1_data[3] = not_1_out ? d3 : 1'bz;  // Controlled_Buffer controlled_buffer_4
  assign ram_1_data[4] = not_1_out ? d4 : 1'bz;  // Controlled_Buffer controlled_buffer_5
  assign ram_1_data[5] = not_1_out ? d5 : 1'bz;  // Controlled_Buffer controlled_buffer_6
  assign ram_1_data[6] = not_1_out ? d6 : 1'bz;  // Controlled_Buffer controlled_buffer_7
  assign ram_1_data[7] = not_1_out ? d7 : 1'bz;  // Controlled_Buffer controlled_buffer_8
  assign q0 = not_2_out ? ram_1_data[0] : 1'bz;  // Controlled_Buffer controlled_buffer_9
  assign q1 = not_2_out ? ram_1_data[1] : 1'bz;  // Controlled_Buffer controlled_buffer_10
  assign q2 = not_2_out ? ram_1_data[2] : 1'bz;  // Controlled_Buffer controlled_buffer_11
  assign q3 = not_2_out ? ram_1_data[3] : 1'bz;  // Controlled_Buffer controlled_buffer_12
  assign q4 = not_2_out ? ram_1_data[4] : 1'bz;  // Controlled_Buffer controlled_buffer_13
  assign q5 = not_2_out ? ram_1_data[5] : 1'bz;  // Controlled_Buffer controlled_buffer_14
  assign q6 = not_2_out ? ram_1_data[6] : 1'bz;  // Controlled_Buffer controlled_buffer_15
  assign q7 = not_2_out ? ram_1_data[7] : 1'bz;  // Controlled_Buffer controlled_buffer_16
endmodule

module Theoretical (
  input  [7:0] in_1,
  input  Clear,
  input  [7:0] in_3,
  input  Clock,
  input  Send,
  input  Request,
  output [7:0] out_7
);

  wire and_1_out, and_2_out, decoder_1_out0, decoder_1_out1, decoder_1_out2, decoder_1_out3, decoder_1_out4,
       decoder_1_out5, decoder_1_out6, decoder_1_out7, nand_1_out, nand_2_out, not_1_out, not_2_out,
       not_4_out, not_5_out, not_6_out, not_7_out, not_8_out, not_11_out, not_12_out, not_13_out, or_1_out,
       or_2_out;
  wire [0:0] not_3_out;
  wire [3:0] counter_1_q, ram_1_data;
  wire [7:4] ram_1_data_2;
  wire [11:4] register_1_q;

  not not_1 (not_1_out, in_3[7]);
  not not_2 (not_2_out, in_3[6]);
  not not_3 (not_3_out[0], Send);
  nand nand_1 (nand_1_out, not_8_out, not_6_out);
  not not_4 (not_4_out, decoder_1_out2);
  not not_5 (not_5_out, decoder_1_out5);
  not not_6 (not_6_out, decoder_1_out0);
  not not_7 (not_7_out, decoder_1_out3);
  not not_8 (not_8_out, decoder_1_out1);
  // NOT_Gate not_9 has open pins: in=decoder_1_out4, out=open
  Decoder #(.select(3), .disabled(0)) decoder_1 (
    .out0(decoder_1_out0), .out1(decoder_1_out1), .out2(decoder_1_out2), .out3(decoder_1_out3),
    .out4(decoder_1_out4), .out5(decoder_1_out5), .out6(decoder_1_out6), .out7(decoder_1_out7),
    .sel({in_3[5:4], not_3_out[0]}), .en(and_1_out));
  and and_1 (and_1_out, not_2_out, not_1_out);
  or or_1 (or_1_out, not_5_out, Send);
  // NOT_Gate not_10 has open pins: in=decoder_1_out6, out=open
  Register register_1 (.D({ram_1_data_2, ram_1_data}), .en(1'b1), .Q(register_1_q), .clk(or_1_out), .clr(Clear));
  Counter #(.width(4), .max('hf)) counter_1 (
    .load(decoder_1_out7), .D(ram_1_data), .count(in_3[0]), .Q(counter_1_q), .clk(and_2_out), .clr(Clear));  // open: carry
  and and_2 (and_2_out, Send, or_2_out);
  RAM #(.addrWidth(15)) ram_1 (
    .addr({in_3[3:1], register_1_q, counter_1_q}), .data({ram_1_data_2, ram_1_data}), .sel(nand_1_out),
    .clk(Send), .ld(not_8_out), .clr(Clear));
  RAM #(.addrWidth(15)) ram_2 (
    .addr({in_3[3:1], register_1_q, counter_1_q}), .data({ram_1_data_2, ram_1_data}), .sel(nand_2_out),
    .clk(Send), .ld(not_7_out), .clr(Clear));
  assign {ram_1_data_2, ram_1_data} = not_11_out ? in_1 : 8'bz;  // Controlled_Buffer controlled_buffer_1
  not not_11 (not_11_out, Send);
  assign out_7 = not_12_out ? {ram_1_data_2, ram_1_data} : 8'bz;  // Controlled_Buffer controlled_buffer_2
  not not_12 (not_12_out, Request);
  nand nand_2 (nand_2_out, not_4_out, not_7_out);
  or or_2 (or_2_out, not_13_out, Clock);
  not not_13 (not_13_out, Send);
endmodule
